// Logisim project HERA_microprocessor.circ as structural Verilog: 23 circuits, main circuit main
module main (
);

  wire branch, CLK, FP_swap, not_1_out, not_2_out, write_flags, write_memory;
  wire [3:0] new_FP, read_register_1, read_register_2, write_register;
  wire [4:0] flags_in, flags_out;
  wire [15:0] FP, FP_alt, FP_in, instruction, memory_access_address, memory_read_value, PC_in, PC_out, R1,
       R2, R3, register_read_value_1, register_read_value_2, SP, SP_alt, write_value;

  Clock clock_1 (.out(CLK));
  not not_1 (not_1_out, branch);
  Hex_Digit_Display hex_digit_display_1 (.value(register_read_value_1[15:12]));  // open: dp
  Hex_Digit_Display hex_digit_display_2 (.value(R1[15:12]));  // open: dp
  Counter #(.width(16), .max('hffff)) counter_1 (
    .load(branch), .D(PC_out), .count(not_1_out), .Q(PC_in), .clk(CLK));  // open: carry, clr
  Hex_Digit_Display hex_digit_display_3 (.value(register_read_value_1[7:4]));  // open: dp
  Hex_Digit_Display hex_digit_display_4 (.value(register_read_value_1[11:8]));  // open: dp
  Hex_Digit_Display hex_digit_display_5 (.value(R1[7:4]));  // open: dp
  Hex_Digit_Display hex_digit_display_6 (.value(R1[11:8]));  // open: dp
  Hex_Digit_Display hex_digit_display_7 (.value(instruction[11:8]));  // open: dp
  Hex_Digit_Display hex_digit_display_8 (.value(instruction[15:12]));  // open: dp
  LED sign (.in(flags_in[0]));
  LED zero (.in(flags_in[1]));
  LED overflow (.in(flags_in[2]));
  LED carry (.in(flags_in[3]));
  LED carry_block (.in(flags_in[4]));
  Hex_Digit_Display hex_digit_display_9 (.value(read_register_1));  // open: dp
  Hex_Digit_Display hex_digit_display_10 (.value(register_read_value_1[3:0]));  // open: dp
  Hex_Digit_Display hex_digit_display_11 (.value(R1[3:0]));  // open: dp
  Hex_Digit_Display hex_digit_display_12 (.value(instruction[7:4]));  // open: dp
  Hex_Digit_Display hex_digit_display_13 (.value(register_read_value_2[15:12]));  // open: dp
  Hex_Digit_Display hex_digit_display_14 (.value(R2[15:12]));  // open: dp
  ROM #(.addrWidth(16), .dataWidth(16)) rom_1 (.addr(PC_in), .data(instruction));  // open: sel
  Hex_Digit_Display hex_digit_display_15 (.value(instruction[3:0]));  // open: dp
  Hex_Digit_Display hex_digit_display_16 (.value(register_read_value_2[11:8]));  // open: dp
  Hex_Digit_Display hex_digit_display_17 (.value(register_read_value_2[7:4]));  // open: dp
  Hex_Digit_Display hex_digit_display_18 (.value(R2[11:8]));  // open: dp
  Hex_Digit_Display hex_digit_display_19 (.value(R2[7:4]));  // open: dp
  LED sign_2 (.in(flags_out[0]));
  LED zero_2 (.in(flags_out[1]));
  LED overflow_2 (.in(flags_out[2]));
  LED carry_2 (.in(flags_out[3]));
  LED carry_block_2 (.in(flags_out[4]));
  Hex_Digit_Display hex_digit_display_20 (.value(read_register_2));  // open: dp
  Hex_Digit_Display hex_digit_display_21 (.value(register_read_value_2[3:0]));  // open: dp
  Hex_Digit_Display hex_digit_display_22 (.value(R2[3:0]));  // open: dp
  flags flags (
    .CLK(CLK), .sign_in(flags_out[0]), .zero_in(flags_out[1]), .overflow_in(flags_out[2]),
    .carry_in(flags_out[3]), .carry_block_in(flags_out[4]), .Write(write_flags), .sign_out(flags_in[0]),
    .zero_out(flags_in[1]), .overflow_out(flags_in[2]), .carry_out(flags_in[3]), .carry_block_out(flags_in[4]));
  Hex_Digit_Display hex_digit_display_23 (.value(write_value[11:8]));  // open: dp
  Hex_Digit_Display hex_digit_display_24 (.value(write_value[15:12]));  // open: dp
  Hex_Digit_Display hex_digit_display_25 (.value(R3[11:8]));  // open: dp
  Hex_Digit_Display hex_digit_display_26 (.value(R3[15:12]));  // open: dp
  LED led_1 (.in(write_flags));
  Hex_Digit_Display hex_digit_display_27 (.value(write_value[7:4]));  // open: dp
  Hex_Digit_Display hex_digit_display_28 (.value(R3[7:4]));  // open: dp
  ALSU ALSU (
    .Instruction(instruction), .flags_in(flags_in), .register_read_value_1(register_read_value_1),
    .register_read_value_2(register_read_value_2), .memory_read_value(memory_read_value),
    .program_counter_in(PC_in), .frame_pointer_in(FP_in), .write_flags(write_flags), .flags_out(flags_out),
    .read_register_1(read_register_1), .read_register_2(read_register_2), .write_register(write_register),
    .write_value(write_value), .memory_access_address(memory_access_address), .write_memory(write_memory),
    .program_counter_out(PC_out), .write_PC(branch), .FP_swap(FP_swap), .new_FP(new_FP));
  Hex_Digit_Display hex_digit_display_29 (.value(write_register));  // open: dp
  Hex_Digit_Display hex_digit_display_30 (.value(write_value[3:0]));  // open: dp
  Hex_Digit_Display hex_digit_display_31 (.value(R3[3:0]));  // open: dp
  register_bank register_bank (
    .read_address_1(read_register_1), .read_address_2(read_register_2), .write_address(write_register),
    .write_data(write_value), .FP_swap(FP_swap), .new_FP(new_FP), .CLK(CLK),
    .read_data_1(register_read_value_1), .read_data_2(register_read_value_2), .R1(R1), .R2(R2), .R3(R3),
    .FP_alt(FP_alt), .SP_alt(SP_alt), .FP(FP), .SP(SP));
  Hex_Digit_Display hex_digit_display_32 (.value(FP_alt[11:8]));  // open: dp
  Hex_Digit_Display hex_digit_display_33 (.value(FP_alt[15:12]));  // open: dp
  Hex_Digit_Display hex_digit_display_34 (.value(FP[11:8]));  // open: dp
  Hex_Digit_Display hex_digit_display_35 (.value(FP[15:12]));  // open: dp
  Hex_Digit_Display hex_digit_display_36 (.value(PC_in[11:8]));  // open: dp
  Hex_Digit_Display hex_digit_display_37 (.value(PC_in[15:12]));  // open: dp
  Hex_Digit_Display hex_digit_display_38 (.value(FP_alt[7:4]));  // open: dp
  Hex_Digit_Display hex_digit_display_39 (.value(FP[7:4]));  // open: dp
  Hex_Digit_Display hex_digit_display_40 (.value(PC_in[7:4]));  // open: dp
  Hex_Digit_Display hex_digit_display_41 (.value(FP_alt[3:0]));  // open: dp
  Hex_Digit_Display hex_digit_display_42 (.value(FP[3:0]));  // open: dp
  Hex_Digit_Display hex_digit_display_43 (.value(PC_in[3:0]));  // open: dp
  Hex_Digit_Display hex_digit_display_44 (.value(SP_alt[15:12]));  // open: dp
  Hex_Digit_Display hex_digit_display_45 (.value(SP_alt[11:8]));  // open: dp
  Hex_Digit_Display hex_digit_display_46 (.value(SP[11:8]));  // open: dp
  Hex_Digit_Display hex_digit_display_47 (.value(SP[15:12]));  // open: dp
  Hex_Digit_Display hex_digit_display_48 (.value(SP_alt[7:4]));  // open: dp
  Hex_Digit_Display hex_digit_display_49 (.value(SP[7:4]));  // open: dp
  Hex_Digit_Display hex_digit_display_50 (.value(SP_alt[3:0]));  // open: dp
  Hex_Digit_Display hex_digit_display_51 (.value(SP[3:0]));  // open: dp
  RAM #(.addrWidth(16), .dataWidth(16), .bus("separate")) ram_1 (
    .addr(memory_access_address), .din(write_value), .data(memory_read_value), .clk(CLK), .ld(not_2_out));  // open: str, sel, clr
  not not_2 (not_2_out, write_memory);

  // Notes on the sheet:
  //   current instruction
  //   contents of rom_1 (hex, n*v repeats v):
  //   f110 f210 3460 c412 3461 c312
  //   program counter
endmodule

module register_bank (
  input  [3:0] read_address_1,
  input  [3:0] read_address_2,
  input  [3:0] write_address,
  input  [15:0] write_data,
  input  FP_swap,
  input  [3:0] new_FP,
  input  CLK,
  output [15:0] read_data_1,
  output [15:0] read_data_2,
  output [15:0] R1,
  output [15:0] R2,
  output [15:0] R3,
  output [15:0] FP_alt,
  output [15:0] SP_alt,
  output [15:0] FP,
  output [15:0] SP
);

  wire FP_write_enable_1, FP_write_enable_2, FP_write_enable_3, FP_write_enable_4, FP_write_enable_5,
       FP_write_enable_6, FP_write_enable_7, FP_write_enable_8, FP_write_enable_9, FP_write_enable_a,
       FP_write_enable_b, FP_write_enable_c, FP_write_enable_d, FP_write_enable_e, FP_write_enable_f,
       or_2_out, or_4_out, or_6_out, or_8_out, or_10_out, or_12_out, or_14_out, or_16_out, or_18_out,
       or_20_out, or_22_out, or_24_out, or_26_out, or_28_out, or_30_out, write_enable_1, write_enable_2,
       write_enable_3, write_enable_4, write_enable_5, write_enable_6, write_enable_7, write_enable_8,
       write_enable_9, write_enable_a, write_enable_b, write_enable_c, write_enable_d, write_enable_e,
       write_enable_f;
  wire [3:0] multiplexer_1_out;
  wire [15:0] FP_write_data_1, FP_write_data_2, FP_write_data_3, FP_write_data_4, FP_write_data_5,
       FP_write_data_6, FP_write_data_7, FP_write_data_8, FP_write_data_9, FP_write_data_a, FP_write_data_b,
       FP_write_data_c, FP_write_data_d, FP_write_data_e, FP_write_data_f, new_FP_value, or_1_out, or_3_out,
       or_5_out, or_7_out, or_9_out, or_11_out, or_13_out, or_15_out, or_17_out, or_19_out, or_21_out,
       or_23_out, or_25_out, or_27_out, or_29_out, value_0, value_4, value_5, value_6, value_7, value_8,
       value_9, value_a, value_b, write_data_1, write_data_2, write_data_3, write_data_4, write_data_5,
       write_data_6, write_data_7, write_data_8, write_data_9, write_data_a, write_data_b, write_data_c,
       write_data_d, write_data_e, write_data_f;

  Demultiplexer #(.select(4), .width(16)) demultiplexer_1 (
    .out1(write_data_1), .out2(write_data_2), .out3(write_data_3), .out4(write_data_4), .out5(write_data_5),
    .out6(write_data_6), .out7(write_data_7), .out8(write_data_8), .out9(write_data_9), .out10(write_data_a),
    .out11(write_data_b), .out12(write_data_c), .out13(write_data_d), .out14(write_data_e),
    .out15(write_data_f), .in(write_data), .sel(write_address));  // open: out0, en
  Demultiplexer #(.select(4), .width(16)) demultiplexer_2 (
    .out1(FP_write_data_1), .out2(FP_write_data_2), .out3(FP_write_data_3), .out4(FP_write_data_4),
    .out5(FP_write_data_5), .out6(FP_write_data_6), .out7(FP_write_data_7), .out8(FP_write_data_8),
    .out9(FP_write_data_9), .out10(FP_write_data_a), .out11(FP_write_data_b), .out12(FP_write_data_c),
    .out13(FP_write_data_d), .out14(FP_write_data_e), .out15(FP_write_data_f), .in(FP), .sel(new_FP));  // open: out0, en
  Decoder #(.select(4)) decoder_1 (
    .out1(write_enable_1), .out2(write_enable_2), .out3(write_enable_3), .out4(write_enable_4),
    .out5(write_enable_5), .out6(write_enable_6), .out7(write_enable_7), .out8(write_enable_8),
    .out9(write_enable_9), .out10(write_enable_a), .out11(write_enable_b), .out12(write_enable_c),
    .out13(write_enable_d), .out14(write_enable_e), .out15(write_enable_f), .sel(write_address));  // open: out0, en
  Decoder #(.select(4)) decoder_2 (
    .out1(FP_write_enable_1), .out2(FP_write_enable_2), .out3(FP_write_enable_3), .out4(FP_write_enable_4),
    .out5(FP_write_enable_5), .out6(FP_write_enable_6), .out7(FP_write_enable_7), .out8(FP_write_enable_8),
    .out9(FP_write_enable_9), .out10(FP_write_enable_a), .out11(FP_write_enable_b),
    .out12(FP_write_enable_c), .out13(FP_write_enable_d), .out14(FP_write_enable_e),
    .out15(FP_write_enable_f), .sel(multiplexer_1_out));  // open: out0, en
  Multiplexer #(.width(4)) multiplexer_1 (
    .in0(4'b0000), .in1(new_FP), .out(multiplexer_1_out), .sel(FP_swap));  // open: en
  assign or_1_out = write_data_1 | FP_write_data_1;  // OR_Gate or_1, 16 bits wide
  or or_2 (or_2_out, write_enable_1, FP_write_enable_1);
  assign or_3_out = write_data_2 | FP_write_data_2;  // OR_Gate or_3, 16 bits wide
  or or_4 (or_4_out, write_enable_2, FP_write_enable_2);
  assign or_5_out = write_data_3 | FP_write_data_3;  // OR_Gate or_5, 16 bits wide
  or or_6 (or_6_out, write_enable_3, FP_write_enable_3);
  assign or_7_out = write_data_4 | FP_write_data_4;  // OR_Gate or_7, 16 bits wide
  or or_8 (or_8_out, write_enable_4, FP_write_enable_4);
  assign or_9_out = write_data_5 | FP_write_data_5;  // OR_Gate or_9, 16 bits wide
  or or_10 (or_10_out, write_enable_5, FP_write_enable_5);
  assign or_11_out = write_data_6 | FP_write_data_6;  // OR_Gate or_11, 16 bits wide
  or or_12 (or_12_out, write_enable_6, FP_write_enable_6);
  assign or_13_out = write_data_7 | FP_write_data_7;  // OR_Gate or_13, 16 bits wide
  or or_14 (or_14_out, write_enable_7, FP_write_enable_7);
  assign or_15_out = write_data_8 | FP_write_data_8;  // OR_Gate or_15, 16 bits wide
  or or_16 (or_16_out, write_enable_8, FP_write_enable_8);
  assign or_17_out = write_data_9 | FP_write_data_9;  // OR_Gate or_17, 16 bits wide
  or or_18 (or_18_out, write_enable_9, FP_write_enable_9);
  assign or_19_out = write_data_a | FP_write_data_a;  // OR_Gate or_19, 16 bits wide
  or or_20 (or_20_out, write_enable_a, FP_write_enable_a);
  assign or_21_out = write_data_b | FP_write_data_b;  // OR_Gate or_21, 16 bits wide
  or or_22 (or_22_out, write_enable_b, FP_write_enable_b);
  assign or_23_out = write_data_c | FP_write_data_c;  // OR_Gate or_23, 16 bits wide
  or or_24 (or_24_out, write_enable_c, FP_write_enable_c);
  assign or_25_out = write_data_d | FP_write_data_d;  // OR_Gate or_25, 16 bits wide
  or or_26 (or_26_out, write_enable_d, FP_write_enable_d);
  assign or_27_out = write_data_e | FP_write_data_e | new_FP_value;  // OR_Gate or_27, 16 bits wide
  or or_28 (or_28_out, write_enable_e, FP_write_enable_e, FP_swap);
  assign or_29_out = write_data_f | FP_write_data_f;  // OR_Gate or_29, 16 bits wide
  or or_30 (or_30_out, write_enable_f, FP_write_enable_f);
  Register #(.width(16)) register_1 (.Q(value_0), .clk(CLK));  // open: D, en, clr
  Register #(.width(16)) register_2 (.D(or_1_out), .en(or_2_out), .Q(R1), .clk(CLK));  // open: clr
  Register #(.width(16)) register_3 (.D(or_3_out), .en(or_4_out), .Q(R2), .clk(CLK));  // open: clr
  Register #(.width(16)) register_4 (.D(or_5_out), .en(or_6_out), .Q(R3), .clk(CLK));  // open: clr
  Register #(.width(16)) register_5 (.D(or_7_out), .en(or_8_out), .Q(value_4), .clk(CLK));  // open: clr
  Register #(.width(16)) register_6 (.D(or_9_out), .en(or_10_out), .Q(value_5), .clk(CLK));  // open: clr
  Register #(.width(16)) register_7 (.D(or_11_out), .en(or_12_out), .Q(value_6), .clk(CLK));  // open: clr
  Register #(.width(16)) register_8 (.D(or_13_out), .en(or_14_out), .Q(value_7), .clk(CLK));  // open: clr
  Register #(.width(16)) register_9 (.D(or_15_out), .en(or_16_out), .Q(value_8), .clk(CLK));  // open: clr
  Register #(.width(16)) register_10 (.D(or_17_out), .en(or_18_out), .Q(value_9), .clk(CLK));  // open: clr
  Register #(.width(16)) register_11 (.D(or_19_out), .en(or_20_out), .Q(value_a), .clk(CLK));  // open: clr
  Register #(.width(16)) register_12 (.D(or_21_out), .en(or_22_out), .Q(value_b), .clk(CLK));  // open: clr
  Register #(.width(16)) register_13 (.D(or_23_out), .en(or_24_out), .Q(FP_alt), .clk(CLK));  // open: clr
  Register #(.width(16)) register_14 (.D(or_25_out), .en(or_26_out), .Q(SP_alt), .clk(CLK));  // open: clr
  Register #(.width(16)) register_15 (.D(or_27_out), .en(or_28_out), .Q(FP), .clk(CLK));  // open: clr
  Register #(.width(16)) register_16 (.D(or_29_out), .en(or_30_out), .Q(SP), .clk(CLK));  // open: clr
  Multiplexer #(.select(4), .width(16)) multiplexer_2 (
    .in0(value_0), .in1(R1), .in2(R2), .in3(R3), .in4(value_4), .in5(value_5), .in6(value_6), .in7(value_7),
    .in8(value_8), .in9(value_9), .in10(value_a), .in11(value_b), .in12(FP_alt), .in13(SP_alt), .in14(FP),
    .in15(SP), .out(read_data_1), .sel(read_address_1));  // open: en
  Multiplexer #(.select(4), .width(16)) multiplexer_3 (
    .in0(value_0), .in1(R1), .in2(R2), .in3(R3), .in4(value_4), .in5(value_5), .in6(value_6), .in7(value_7),
    .in8(value_8), .in9(value_9), .in10(value_a), .in11(value_b), .in12(FP_alt), .in13(SP_alt), .in14(FP),
    .in15(SP), .out(read_data_2), .sel(read_address_2));  // open: en
  Multiplexer #(.select(4), .width(16)) multiplexer_4 (
    .in0(value_0), .in1(R1), .in2(R2), .in3(R3), .in4(value_4), .in5(value_5), .in6(value_6), .in7(value_7),
    .in8(value_8), .in9(value_9), .in10(value_a), .in11(value_b), .in12(FP_alt), .in13(SP_alt), .in14(FP),
    .in15(SP), .out(new_FP_value), .sel(new_FP));  // open: en

  // Other names for the same wires on the sheet: ra1[3:0] = read_address_1; ra2[3:0] = read_address_2;
  //   value_1[15:0] = R1; value_2[15:0] = R2; value_3[15:0] = R3; value_c[15:0] = FP_alt; value_d[15:0] = SP_alt;
  //   value_e[15:0] = FP; value_f[15:0] = SP; wa[3:0] = write_address
endmodule

module flags (
  input  CLK,
  input  sign_in,
  input  zero_in,
  input  overflow_in,
  input  carry_in,
  input  carry_block_in,
  input  Write,
  output sign_out,
  output zero_out,
  output overflow_out,
  output carry_out,
  output carry_block_out
);

  D_Flip_Flop d_ff_1 (.clk(CLK), .D(sign_in), .Q(sign_out), .en(Write));  // open: Qn, preset, reset
  D_Flip_Flop d_ff_2 (.clk(CLK), .D(zero_in), .Q(zero_out), .en(Write));  // open: Qn, preset, reset
  D_Flip_Flop d_ff_3 (.clk(CLK), .D(overflow_in), .Q(overflow_out), .en(Write));  // open: Qn, preset, reset
  D_Flip_Flop d_ff_4 (.clk(CLK), .D(carry_in), .Q(carry_out), .en(Write));  // open: Qn, preset, reset
  D_Flip_Flop d_ff_5 (.clk(CLK), .D(carry_block_in), .Q(carry_block_out), .en(Write));  // open: Qn, preset, reset
endmodule

module ALSU (
  input  [15:0] Instruction,
  input  [4:0] flags_in,
  input  [15:0] register_read_value_1,
  input  [15:0] register_read_value_2,
  input  [15:0] memory_read_value,
  input  [15:0] program_counter_in,
  input  [15:0] frame_pointer_in,
  output write_flags,
  output [4:0] flags_out,
  output [3:0] read_register_1,
  output [3:0] read_register_2,
  output [3:0] write_register,
  output [15:0] write_value,
  output [15:0] memory_access_address,
  output write_memory,
  output [15:0] program_counter_out,
  output write_PC,
  output FP_swap,
  output [3:0] new_FP
);

  wire _4, _6, _11, _12, ADD, AND, arithmetic_1_write_flags, AShift, ashift_1_write_flags, BRANCH,
       branch_1_write_flags, call_return_1_write_flags, FON_FF, fon_ff_1_write_flags, FSET,
       fset_1_write_flags, INC_DEC, inc_dec_1_write_flags, LOAD, load_1_write_flags, logic_1_write_flags,
       LShift, LShift8, lshift_1_write_flags, MUL, OR, or_1_out, or_2_out, RSTRF, rstrf_1_write_flags, SAVEF,
       savef_1_write_flags, SET, set_1_write_flags, store_1_write_flags, SUB, XOR;
  wire [3:0] _0_3, _4_7, _8_11, arithmetic_1_read_register_1, arithmetic_1_read_register_2,
       arithmetic_1_write_register, ashift_1_read_register_1, ashift_1_read_register_2,
       ashift_1_write_register, branch_1_read_register_1, branch_1_read_register_2, branch_1_write_register,
       call_return_1_read_register_1, call_return_1_read_register_2, call_return_1_write_register,
       fon_ff_1_read_register_1, fon_ff_1_read_register_2, fon_ff_1_write_register, fset_1_read_register_1,
       fset_1_read_register_2, fset_1_write_register, inc_dec_1_read_register_1, inc_dec_1_read_register_2,
       inc_dec_1_write_register, load_1_read_register_1, load_1_read_register_2, load_1_write_register,
       logic_1_read_register_1, logic_1_read_register_2, logic_1_write_register, lshift_1_read_register_1,
       lshift_1_read_register_2, lshift_1_write_register, rstrf_1_read_register_1, rstrf_1_read_register_2,
       rstrf_1_write_register, savef_1_read_register_1, savef_1_read_register_2, savef_1_write_register,
       set_1_read_register_1, set_1_read_register_2, set_1_write_register, store_1_read_register_1,
       store_1_read_register_2, store_1_write_register;
  wire [4:0] arithmetic_1_flags_out, ashift_1_flags_out, branch_1_flags_out, call_return_1_flags_out,
       fon_ff_1_flags_out, fset_1_flags_out, inc_dec_1_flags_out, load_1_flags_out, logic_1_flags_out,
       lshift_1_flags_out, rstrf_1_flags_out, savef_1_flags_out, set_1_flag_values, store_1_flags_out;
  wire [5:0] _0_5, ARITHMETIC_flags_info, AShift_flags_info, FON_FF_flags_info, FSET_flags_info,
       INC_DEC_flags_info, LOAD_flags_info, LOGIC_flags_info, LShift_flags_info, RSTRF_flags_info,
       STORE_flags_info;
  wire [7:0] _0_7;
  wire [15:0] arithmetic_1_write_value, ashift_1_write_value, branch_1_write_value, BRANCH_PC_out,
       call_return_1_write_value, CALL_RETURN_PC_out, fon_ff_1_write_value, fset_1_write_value,
       inc_dec_1_write_value, load_1_write_value, LOAD_memory_access_address, logic_1_write_value,
       lshift_1_write_value, rstrf_1_write_value, savef_1_write_value, set_1_write_value,
       store_1_write_value, STORE_memory_access_address;
  wire [31:0] ARITHMETIC_register_info, AShift_register_info, BRANCH_register_info,
       CALL_RETURN_register_info, INC_DEC_register_info, LOAD_register_info, LOGIC_register_info,
       LShift_register_info, or_4_out, RSTRF_register_info, SAVEF_register_info, SET_register_info,
       STORE_register_info;

  op_selector op_selector_1 (
    .instruction(Instruction), .SET(SET), .AND(AND), .OR(OR), .XOR(XOR), .ADD(ADD), .SUB(SUB), .MUL(MUL),
    .LShift(LShift), .LShift8(LShift8), .AShift(AShift), .SAVEF(SAVEF), .RSTRF(RSTRF), .FON_FF(FON_FF),
    .FSET(FSET), .INC_DEC(INC_DEC), .LOAD(LOAD), .STORE(write_memory), .BRANCH(BRANCH), .CALL_RETURN(FP_swap));
  data_splitter data_splitter_1 (
    .instruction(Instruction), ._0_3(_0_3), ._4_7(_4_7), ._8_11(_8_11), ._0_7(_0_7), ._0_5(_0_5), ._12(_12),
    ._6(_6), ._4(_4), ._11(_11));
  SET set_1 (
    .l_h(_12), .d(_8_11), .v(_0_7), .read_value(register_read_value_1), .write_flags(set_1_write_flags),
    .flag_values(set_1_flag_values), .read_register_1(set_1_read_register_1),
    .read_register_2(set_1_read_register_2), .write_register(set_1_write_register),
    .write_value(set_1_write_value));
  LOGIC logic_1 (
    .d(_8_11), .a(_4_7), .b(_0_3), .read_value_1(register_read_value_1),
    .read_value_2(register_read_value_2), .AND(AND), .OR(OR), .XOR(XOR), .flags_in(flags_in),
    .write_flags(logic_1_write_flags), .flags_out(logic_1_flags_out),
    .read_register_1(logic_1_read_register_1), .read_register_2(logic_1_read_register_2),
    .write_register(logic_1_write_register), .write_value(logic_1_write_value));
  packer packer_1 (
    .enable(SET), .write_flags(set_1_write_flags), .flags_out(set_1_flag_values),
    .read_register_1(set_1_read_register_1), .read_register_2(set_1_read_register_2),
    .write_register(set_1_write_register), .write_value(set_1_write_value), .register_info(SET_register_info));  // open: flag_info
  or or_1 (or_1_out, AND, OR, XOR);
  packer packer_2 (
    .enable(or_1_out), .write_flags(logic_1_write_flags), .flags_out(logic_1_flags_out),
    .read_register_1(logic_1_read_register_1), .read_register_2(logic_1_read_register_2),
    .write_register(logic_1_write_register), .write_value(logic_1_write_value), .flag_info(LOGIC_flags_info),
    .register_info(LOGIC_register_info));
  or or_2 (or_2_out, ADD, SUB, MUL);
  ARITHMETIC arithmetic_1 (
    .d(_8_11), .a(_4_7), .b(_0_3), .read_value_1(register_read_value_1),
    .read_value_2(register_read_value_2), .ADD(ADD), .SUB(SUB), .MUL(MUL), .flags_in(flags_in),
    .write_flags(arithmetic_1_write_flags), .flags_out(arithmetic_1_flags_out),
    .read_register_1(arithmetic_1_read_register_1), .read_register_2(arithmetic_1_read_register_2),
    .write_register(arithmetic_1_write_register), .write_value(arithmetic_1_write_value));
  packer packer_3 (
    .enable(or_2_out), .write_flags(arithmetic_1_write_flags), .flags_out(arithmetic_1_flags_out),
    .read_register_1(arithmetic_1_read_register_1), .read_register_2(arithmetic_1_read_register_2),
    .write_register(arithmetic_1_write_register), .write_value(arithmetic_1_write_value),
    .flag_info(ARITHMETIC_flags_info), .register_info(ARITHMETIC_register_info));
  LShift lshift_1 (
    .d(_8_11), .b(_0_3), .read_value(register_read_value_1), .right(_4), .flags_in(flags_in),
    .write_flags(lshift_1_write_flags), .flags_out(lshift_1_flags_out),
    .read_register_1(lshift_1_read_register_1), .read_register_2(lshift_1_read_register_2),
    .write_register(lshift_1_write_register), .write_value(lshift_1_write_value));
  packer packer_4 (
    .enable(LShift), .write_flags(lshift_1_write_flags), .flags_out(lshift_1_flags_out),
    .read_register_1(lshift_1_read_register_1), .read_register_2(lshift_1_read_register_2),
    .write_register(lshift_1_write_register), .write_value(lshift_1_write_value),
    .flag_info(LShift_flags_info), .register_info(LShift_register_info));
  AShift ashift_1 (
    .d(_8_11), .b(_0_3), .read_value(register_read_value_1), .right(_4), .flags_in(flags_in),
    .write_flags(ashift_1_write_flags), .flags_out(ashift_1_flags_out),
    .read_register_1(ashift_1_read_register_1), .read_register_2(ashift_1_read_register_2),
    .write_register(ashift_1_write_register), .write_value(ashift_1_write_value));
  packer packer_5 (
    .enable(AShift), .write_flags(ashift_1_write_flags), .flags_out(ashift_1_flags_out),
    .read_register_1(ashift_1_read_register_1), .read_register_2(ashift_1_read_register_2),
    .write_register(ashift_1_write_register), .write_value(ashift_1_write_value),
    .flag_info(AShift_flags_info), .register_info(AShift_register_info));
  SAVEF savef_1 (
    .d(_8_11), .flags_in(flags_in), .write_flags(savef_1_write_flags), .flags_out(savef_1_flags_out),
    .read_register_1(savef_1_read_register_1), .read_register_2(savef_1_read_register_2),
    .write_register(savef_1_write_register), .write_value(savef_1_write_value));
  packer packer_6 (
    .enable(SAVEF), .write_flags(savef_1_write_flags), .flags_out(savef_1_flags_out),
    .read_register_1(savef_1_read_register_1), .read_register_2(savef_1_read_register_2),
    .write_register(savef_1_write_register), .write_value(savef_1_write_value),
    .register_info(SAVEF_register_info));  // open: flag_info
  RSTRF rstrf_1 (
    .d(_8_11), .read_value(register_read_value_1), .write_flags(rstrf_1_write_flags),
    .flags_out(rstrf_1_flags_out), .read_register_1(rstrf_1_read_register_1),
    .read_register_2(rstrf_1_read_register_2), .write_register(rstrf_1_write_register),
    .write_value(rstrf_1_write_value));
  packer packer_7 (
    .enable(RSTRF), .write_flags(rstrf_1_write_flags), .flags_out(rstrf_1_flags_out),
    .read_register_1(rstrf_1_read_register_1), .read_register_2(rstrf_1_read_register_2),
    .write_register(rstrf_1_write_register), .write_value(rstrf_1_write_value), .flag_info(RSTRF_flags_info),
    .register_info(RSTRF_register_info));
  FON_FF fon_ff_1 (
    ._0_3(_0_3), ._8_11(_8_11), .flags_in(flags_in), .write_flags(fon_ff_1_write_flags),
    .flags_out(fon_ff_1_flags_out), .read_register_1(fon_ff_1_read_register_1),
    .read_register_2(fon_ff_1_read_register_2), .write_register(fon_ff_1_write_register),
    .write_value(fon_ff_1_write_value));
  packer packer_8 (
    .enable(FON_FF), .write_flags(fon_ff_1_write_flags), .flags_out(fon_ff_1_flags_out),
    .read_register_1(fon_ff_1_read_register_1), .read_register_2(fon_ff_1_read_register_2),
    .write_register(fon_ff_1_write_register), .write_value(fon_ff_1_write_value),
    .flag_info(FON_FF_flags_info));  // open: register_info
  FSET fset_1 (
    ._0_3(_0_3), ._8_11(_8_11), .flags_in(flags_in), .write_flags(fset_1_write_flags),
    .flags_out(fset_1_flags_out), .read_register_1(fset_1_read_register_1),
    .read_register_2(fset_1_read_register_2), .write_register(fset_1_write_register),
    .write_value(fset_1_write_value));
  packer packer_9 (
    .enable(FSET), .write_flags(fset_1_write_flags), .flags_out(fset_1_flags_out),
    .read_register_1(fset_1_read_register_1), .read_register_2(fset_1_read_register_2),
    .write_register(fset_1_write_register), .write_value(fset_1_write_value), .flag_info(FSET_flags_info));  // open: register_info
  INC_DEC inc_dec_1 (
    .d(_8_11), .epsilon(_0_5), .DEC(_6), .flags_in(flags_in), .register_read_value_1(register_read_value_1),
    .write_flags(inc_dec_1_write_flags), .flags_out(inc_dec_1_flags_out),
    .read_register_1(inc_dec_1_read_register_1), .read_register_2(inc_dec_1_read_register_2),
    .write_register(inc_dec_1_write_register), .write_value(inc_dec_1_write_value));
  packer packer_10 (
    .enable(INC_DEC), .write_flags(inc_dec_1_write_flags), .flags_out(inc_dec_1_flags_out),
    .read_register_1(inc_dec_1_read_register_1), .read_register_2(inc_dec_1_read_register_2),
    .write_register(inc_dec_1_write_register), .write_value(inc_dec_1_write_value),
    .flag_info(INC_DEC_flags_info), .register_info(INC_DEC_register_info));
  LOAD load_1 (
    .d(_8_11), .b(_0_3), .o({_12, _4_7}), .flags_in(flags_in), .register_read_value(register_read_value_1),
    .memory_read_value(memory_read_value), .write_flags(load_1_write_flags), .flags_out(load_1_flags_out),
    .read_register_1(load_1_read_register_1), .read_register_2(load_1_read_register_2),
    .write_register(load_1_write_register), .write_value(load_1_write_value),
    .memory_access_address(LOAD_memory_access_address));
  packer packer_11 (
    .enable(LOAD), .write_flags(load_1_write_flags), .flags_out(load_1_flags_out),
    .read_register_1(load_1_read_register_1), .read_register_2(load_1_read_register_2),
    .write_register(load_1_write_register), .write_value(load_1_write_value), .flag_info(LOAD_flags_info),
    .register_info(LOAD_register_info));
  STORE store_1 (
    .d(_8_11), .b(_0_3), .o({_12, _4_7}), .register_read_value_1(register_read_value_1),
    .register_read_value_2(register_read_value_2), .write_flags(store_1_write_flags),
    .flags_out(store_1_flags_out), .read_register_1(store_1_read_register_1),
    .read_register_2(store_1_read_register_2), .write_register(store_1_write_register),
    .write_value(store_1_write_value), .memory_access_address(STORE_memory_access_address));
  packer packer_12 (
    .enable(write_memory), .write_flags(store_1_write_flags), .flags_out(store_1_flags_out),
    .read_register_1(store_1_read_register_1), .read_register_2(store_1_read_register_2),
    .write_register(store_1_write_register), .write_value(store_1_write_value), .flag_info(STORE_flags_info),
    .register_info(STORE_register_info));
  BRANCH branch_1 (
    .ABSOLUTE(_12), .CONDITION_CODE(_8_11), .b(_0_3), .o({_4_7, _0_3}), .flags_in(flags_in),
    .program_counter_in(program_counter_in), .register_read_value(register_read_value_1),
    .write_flags(branch_1_write_flags), .flags_out(branch_1_flags_out),
    .read_register_1(branch_1_read_register_1), .read_register_2(branch_1_read_register_2),
    .write_register(branch_1_write_register), .write_value(branch_1_write_value), .PC_out(BRANCH_PC_out));
  packer packer_13 (
    .enable(BRANCH), .write_flags(branch_1_write_flags), .flags_out(branch_1_flags_out),
    .read_register_1(branch_1_read_register_1), .read_register_2(branch_1_read_register_2),
    .write_register(branch_1_write_register), .write_value(branch_1_write_value),
    .register_info(BRANCH_register_info));  // open: flag_info
  CALL_RETURN call_return_1 (
    .b(_0_3), .program_counter_in(program_counter_in), .register_read_value(register_read_value_1),
    .write_flags(call_return_1_write_flags), .flags_out(call_return_1_flags_out),
    .read_register_1(call_return_1_read_register_1), .read_register_2(call_return_1_read_register_2),
    .write_register(call_return_1_write_register), .write_value(call_return_1_write_value),
    .PC_out(CALL_RETURN_PC_out));
  packer packer_14 (
    .enable(FP_swap), .write_flags(call_return_1_write_flags), .flags_out(call_return_1_flags_out),
    .read_register_1(call_return_1_read_register_1), .read_register_2(call_return_1_read_register_2),
    .write_register(call_return_1_write_register), .write_value(call_return_1_write_value),
    .register_info(CALL_RETURN_register_info));  // open: flag_info
  assign {flags_out, write_flags} = LOGIC_flags_info | ARITHMETIC_flags_info | LShift_flags_info | AShift_flags_info | RSTRF_flags_info | FON_FF_flags_info | FSET_flags_info | INC_DEC_flags_info | LOAD_flags_info | STORE_flags_info;  // OR_Gate or_3, 6 bits wide
  assign or_4_out = SET_register_info | LOGIC_register_info | ARITHMETIC_register_info | LShift_register_info | AShift_register_info | SAVEF_register_info | RSTRF_register_info | INC_DEC_register_info | LOAD_register_info | STORE_register_info | BRANCH_register_info | CALL_RETURN_register_info;  // OR_Gate or_4, 32 bits wide
  or or_5 (write_PC, BRANCH, FP_swap);
  Multiplexer #(.width(4)) multiplexer_1 (.in0(4'b0000), .in1(_4_7), .out(new_FP), .sel(FP_swap));  // open: en
  register_info_unpacker register_info_unpacker_1 (
    .register_info(or_4_out), .read_register_1(read_register_1), .read_register_2(read_register_2),
    .write_register(write_register), .write_value(write_value));
  Multiplexer #(.select(2), .width(16)) multiplexer_2 (
    .in1(LOAD_memory_access_address), .in2(STORE_memory_access_address), .out(memory_access_address),
    .sel({write_memory, LOAD}));  // open: in0, in3, en
  Multiplexer #(.width(16)) multiplexer_3 (
    .in0(BRANCH_PC_out), .in1(CALL_RETURN_PC_out), .out(program_counter_out), .sel(FP_swap));  // open: en

  // Other names for the same wires on the sheet: STORE = write_memory; CALL_RETURN = FP_swap;
  //   fp[15:0] = frame_pointer_in; mv[15:0] = memory_read_value; PC_in[15:0] = program_counter_in;
  //   rv1[15:0] = register_read_value_1; rv2[15:0] = register_read_value_2

  // Notes on the sheet:
  //   modules are named for their corresponding HERA command
  //   their inputs are abbreviated as in the HERA documentation
  //   hi
endmodule

module SET (
  input  l_h,
  input  [3:0] d,
  input  [7:0] v,
  input  [15:0] read_value,
  output write_flags,
  output [4:0] flag_values,
  output [3:0] read_register_1,
  output [3:0] read_register_2,
  output [3:0] write_register,
  output [15:0] write_value
);

  wire [15:0] and_1_out, and_2_out, bit_extender_1_out;

  assign bit_extender_1_out = {{15{l_h}}, l_h};  // Bit_Extender bit_extender_1
  assign and_1_out = bit_extender_1_out & {v, read_value[7:0]};  // AND_Gate and_1, 16 bits wide
  assign and_2_out = {{8{1'b0}}, v} & ~bit_extender_1_out;  // AND_Gate and_2, 16 bits wide
  assign write_value = and_1_out | and_2_out;  // OR_Gate or_1, 16 bits wide

  assign flag_values = {5{1'b0}};
  assign read_register_1 = d;
  assign read_register_2 = 4'b0000;
  assign write_flags = 1'b0;
  assign write_register = d;
endmodule

module packer (
  input  enable,
  input  write_flags,
  input  [4:0] flags_out,
  input  [3:0] read_register_1,
  input  [3:0] read_register_2,
  input  [3:0] write_register,
  input  [15:0] write_value,
  output [5:0] flag_info,
  output [31:0] register_info
);

  wire [5:0] bit_extender_1_out;
  wire [31:0] bit_extender_2_out;

  assign bit_extender_1_out = {{5{enable}}, enable};  // Bit_Extender bit_extender_1
  assign bit_extender_2_out = {{31{enable}}, enable};  // Bit_Extender bit_extender_2
  assign flag_info = bit_extender_1_out & {flags_out, write_flags};  // AND_Gate and_1, 6 bits wide
  assign register_info = bit_extender_2_out & {write_value, write_register, read_register_2, read_register_1, 4'b0000};  // AND_Gate and_2, 32 bits wide
endmodule

module register_info_unpacker (
  input  [31:0] register_info,
  output [3:0] read_register_1,
  output [3:0] read_register_2,
  output [3:0] write_register,
  output [15:0] write_value
);


  assign read_register_1 = register_info[7:4];
  assign read_register_2 = register_info[11:8];
  assign write_register = register_info[15:12];
  assign write_value = register_info[31:16];
endmodule

module op_selector (
  input  [15:0] instruction,
  output SET,
  output AND,
  output OR,
  output XOR,
  output ADD,
  output SUB,
  output MUL,
  output LShift,
  output LShift8,
  output AShift,
  output SAVEF,
  output RSTRF,
  output FON_FF,
  output FSET,
  output INC_DEC,
  output LOAD,
  output STORE,
  output BRANCH,
  output CALL_RETURN
);

  wire and_8_out, and_12_out, and_13_out, and_14_out, and_15_out, and_16_out, and_17_out, and_18_out;

  and and_1 (SET, instruction[13], instruction[14], instruction[15]);
  and and_2 (AND, ~instruction[12], ~instruction[13], ~instruction[14], instruction[15]);  // AND_Gate
  and and_3 (OR, instruction[12], ~instruction[13], ~instruction[14], instruction[15]);  // AND_Gate
  and and_4 (XOR, instruction[12], ~instruction[13], instruction[14], instruction[15]);  // AND_Gate
  and and_5 (ADD, ~instruction[12], instruction[13], ~instruction[14], instruction[15]);  // AND_Gate
  and and_6 (SUB, instruction[12], instruction[13], ~instruction[14], instruction[15]);  // AND_Gate
  and and_7 (MUL, ~instruction[12], ~instruction[13], instruction[14], instruction[15]);  // AND_Gate
  and and_8 (and_8_out, instruction[12], instruction[13], ~instruction[14], ~instruction[15]);  // AND_Gate
  and and_9 (LOAD, ~instruction[13], instruction[14], ~instruction[15]);  // AND_Gate
  and and_10 (STORE, instruction[13], instruction[14], ~instruction[15]);  // AND_Gate
  and and_11 (BRANCH, ~instruction[13], ~instruction[14], ~instruction[15]);  // AND_Gate
  and and_12 (and_12_out, ~instruction[5], ~instruction[6], ~instruction[7]);  // AND_Gate
  and and_13 (and_13_out, instruction[5], ~instruction[6], ~instruction[7]);  // AND_Gate
  and and_14 (and_14_out, ~instruction[5], instruction[6], ~instruction[7]);  // AND_Gate
  and and_15 (and_15_out, ~instruction[0], ~instruction[1], ~instruction[2], ~instruction[3], instruction[4], instruction[5], instruction[6], ~instruction[7]);  // AND_Gate
  and and_16 (and_16_out, ~instruction[0], ~instruction[1], ~instruction[2], instruction[3], instruction[4], instruction[5], instruction[6], ~instruction[7]);  // AND_Gate
  and and_17 (and_17_out, ~instruction[4], instruction[5], instruction[6], ~instruction[7], ~instruction[9], ~instruction[10]);  // AND_Gate
  and and_18 (and_18_out, ~instruction[4], instruction[5], instruction[6], ~instruction[7], ~instruction[9], instruction[10]);  // AND_Gate
  and and_19 (LShift, and_8_out, and_12_out);
  and and_20 (LShift8, and_8_out, and_13_out);
  and and_21 (AShift, and_8_out, and_14_out);
  and and_22 (SAVEF, and_8_out, and_15_out);
  and and_23 (RSTRF, and_8_out, and_16_out);
  and and_24 (FON_FF, and_8_out, and_17_out);
  and and_25 (FSET, and_8_out, and_18_out);
  and and_26 (INC_DEC, instruction[7], instruction[12], instruction[13], ~instruction[14], ~instruction[15]);  // AND_Gate
  and and_27 (CALL_RETURN, ~instruction[9], ~instruction[10], ~instruction[11], ~instruction[12], instruction[13], ~instruction[14], ~instruction[15]);  // AND_Gate
endmodule

module data_splitter (
  input  [15:0] instruction,
  output [3:0] _0_3,
  output [3:0] _4_7,
  output [3:0] _8_11,
  output [7:0] _0_7,
  output [5:0] _0_5,
  output _12,
  output _6,
  output _4,
  output _11
);


  assign _0_3 = instruction[3:0];
  assign _0_5 = instruction[5:0];
  assign _0_7 = instruction[7:0];
  assign _4 = instruction[4];
  assign _4_7 = instruction[7:4];
  assign _6 = instruction[6];
  assign _8_11 = instruction[11:8];
  assign _11 = instruction[11];
  assign _12 = instruction[12];
endmodule

module LOGIC (
  input  [3:0] d,
  input  [3:0] a,
  input  [3:0] b,
  input  [15:0] read_value_1,
  input  [15:0] read_value_2,
  input  AND,
  input  OR,
  input  XOR,
  input  [4:0] flags_in,
  output write_flags,
  output [4:0] flags_out,
  output [3:0] read_register_1,
  output [3:0] read_register_2,
  output [3:0] write_register,
  output [15:0] write_value
);

  wire [1:0] or_1_out;
  wire [15:0] and_1_out, or_3_out, xor_1_out;

  or or_1 (or_1_out[0], AND, XOR);
  or or_2 (or_1_out[1], XOR, OR);
  assign and_1_out = read_value_1 & read_value_2;  // AND_Gate and_1, 16 bits wide
  Multiplexer #(.select(2), .width(16)) multiplexer_1 (
    .in0({16{1'b0}}), .in1(and_1_out), .in2(or_3_out), .in3(xor_1_out), .out(write_value), .sel(or_1_out));  // open: en
  assign or_3_out = read_value_1 | read_value_2;  // OR_Gate or_3, 16 bits wide
  assign xor_1_out = read_value_1 ^ read_value_2;  // XOR_Gate xor_1, 16 bits wide
  zero_sign zero_sign_1 (.in_1(write_value), .zero(flags_out[1]), .sign(flags_out[0]));

  assign flags_out[4:2] = flags_in[4:2];
  assign read_register_1 = a;
  assign read_register_2 = b;
  assign write_flags = 1'b1;
  assign write_register = d;

  // Other names for the same wires on the sheet: sign_out = flags_out[0]; zero_out = flags_out[1];
  //   rv1[15:0] = read_value_1; rv2[15:0] = read_value_2
endmodule

module ARITHMETIC (
  input  [3:0] d,
  input  [3:0] a,
  input  [3:0] b,
  input  [15:0] read_value_1,
  input  [15:0] read_value_2,
  input  ADD,
  input  SUB,
  input  MUL,
  input  [4:0] flags_in,
  output write_flags,
  output [4:0] flags_out,
  output [3:0] read_register_1,
  output [3:0] read_register_2,
  output [3:0] write_register,
  output [15:0] write_value
);

  wire adder_1_cout, and_1_out, and_2_out, and_3_out, and_4_out, comparator_1_eq, comparator_2_eq, not_1_out,
       not_2_out, subtractor_1_bout, xnor_1_out, xor_1_out, xor_2_out, xor_3_out, xor_4_out,
       zero_sign_1_sign, zero_sign_1_zero;
  wire [1:0] OP;
  wire [15:0] adder_1_out, multiplexer_1_out, multiplier_1_cout, multiplier_1_out, subtractor_1_out;

  or or_1 (OP[0], ADD, SUB);
  or or_2 (OP[1], SUB, MUL);
  xor xor_1 (xor_1_out, read_value_2[15], flags_in[0]);
  and and_1 (and_1_out, flags_in[3], ~flags_in[4]);  // AND_Gate
  and and_2 (and_2_out, ~flags_in[4], ~flags_in[3]);  // AND_Gate
  Adder #(.width(16)) adder_1 (
    .a(read_value_1), .b(read_value_2), .out(adder_1_out), .cin(and_1_out), .cout(adder_1_cout));
  Multiplier #(.width(16)) multiplier_1 (
    .a(read_value_1), .b(read_value_2), .out(multiplier_1_out), .cout(multiplier_1_cout));  // open: cin
  Comparator #(.width(16)) comparator_1 (.a(multiplier_1_cout), .b({16{1'b0}}), .eq(comparator_1_eq));  // open: gt, lt
  Subtractor #(.width(16)) subtractor_1 (
    .a(read_value_1), .b(read_value_2), .out(subtractor_1_out), .bin(and_2_out), .bout(subtractor_1_bout));
  xor xor_2 (xor_2_out, write_value[15], xor_1_out);
  xnor xnor_1 (xnor_1_out, xor_1_out, read_value_1[15]);
  xor xor_3 (xor_3_out, multiplier_1_cout[15], read_value_1[15]);
  and and_3 (and_3_out, xor_2_out, xnor_1_out);
  Multiplexer #(.width(16)) multiplexer_1 (
    .in0(multiplier_1_out), .in1(multiplier_1_cout), .out(multiplexer_1_out), .sel(flags_in[0]));  // open: en
  not not_1 (not_1_out, subtractor_1_bout);
  xor xor_4 (xor_4_out, write_value[15], xor_3_out);
  Multiplexer #(.select(2), .width(16)) multiplexer_2 (
    .in0({16{1'b0}}), .in1(adder_1_out), .in2(multiplexer_1_out), .in3(subtractor_1_out), .out(write_value),
    .sel(OP));  // open: en
  not not_2 (not_2_out, comparator_1_eq);
  Multiplexer #(.select(2)) multiplexer_3 (
    .in0(1'b0), .in1(and_3_out), .in2(xor_4_out), .in3(and_3_out), .out(flags_out[2]), .sel(OP));  // open: en
  Multiplexer #(.select(2)) multiplexer_4 (
    .in0(1'b0), .in1(adder_1_cout), .in2(not_2_out), .in3(not_1_out), .out(flags_out[3]), .sel(OP));  // open: en
  Comparator #(.width(16)) comparator_2 (.a(multiplexer_1_out), .b({16{1'b0}}), .eq(comparator_2_eq));  // open: gt, lt
  zero_sign zero_sign_1 (.in_1(write_value), .zero(zero_sign_1_zero), .sign(zero_sign_1_sign));
  and and_4 (and_4_out, comparator_2_eq, comparator_1_eq);
  Multiplexer #(.select(2)) multiplexer_5 (
    .in0(1'b0), .in1(zero_sign_1_zero), .in2(and_4_out), .in3(zero_sign_1_zero), .out(flags_out[1]), .sel(OP));  // open: en
  Multiplexer #(.select(2)) multiplexer_6 (
    .in0(1'b0), .in1(zero_sign_1_sign), .in2(multiplier_1_cout[15]), .in3(zero_sign_1_sign),
    .out(flags_out[0]), .sel(OP));  // open: en

  assign flags_out[4] = flags_in[4];
  assign read_register_1 = a;
  assign read_register_2 = b;
  assign write_flags = 1'b1;
  assign write_register = d;

  // Other names for the same wires on the sheet: sign_in = flags_in[0]; overflow_in = flags_in[2];
  //   carry_in = flags_in[3]; carry_block_in = flags_in[4]; sign_out = flags_out[0]; zero_out = flags_out[1];
  //   overflow_out = flags_out[2]; carry_out = flags_out[3]; rv1[15:0] = read_value_1; rv2[15:0] = read_value_2
endmodule

module zero_sign (
  input  [15:0] in_1,
  output zero,
  output sign
);

  nor nor_1 (zero, in_1[0], in_1[1], in_1[2], in_1[3], in_1[4], in_1[5], in_1[6], in_1[7], in_1[9], in_1[10], in_1[11], in_1[12], in_1[13], in_1[14], in_1[15], in_1[8]);

  assign sign = in_1[15];
endmodule

module LShift (
  input  [3:0] d,
  input  [3:0] b,
  input  [15:0] read_value,
  input  right,
  input  [4:0] flags_in,
  output write_flags,
  output [4:0] flags_out,
  output [3:0] read_register_1,
  output [3:0] read_register_2,
  output [3:0] write_register,
  output [15:0] write_value
);

  wire [0:0] and_1_out;

  and and_1 (and_1_out[0], flags_in[3], ~flags_in[4]);  // AND_Gate
  Multiplexer #(.width(16)) multiplexer_1 (
    .in0({read_value[14:0], and_1_out[0]}), .in1({and_1_out[0], read_value[15:1]}), .out(write_value),
    .sel(right));  // open: en
  Multiplexer multiplexer_2 (.in0(read_value[15]), .in1(read_value[0]), .out(flags_out[3]), .sel(right));  // open: en
  zero_sign zero_sign_1 (.in_1(write_value), .zero(flags_out[1]), .sign(flags_out[0]));

  assign {flags_out[4], flags_out[2]} = {flags_in[4], flags_in[2]};
  assign read_register_1 = b;
  assign read_register_2 = 4'b0000;
  assign write_flags = 1'b1;
  assign write_register = d;

  // Other names for the same wires on the sheet: rv[15:0] = read_value; carry_in = flags_in[3];
  //   sign_out = flags_out[0]; zero_out = flags_out[1]; overflow_in = flags_in[2]; carry_out = flags_out[3];
  //   carry_block_in = flags_in[4]
endmodule

module AShift (
  input  [3:0] d,
  input  [3:0] b,
  input  [15:0] read_value,
  input  right,
  input  [4:0] flags_in,
  output write_flags,
  output [4:0] flags_out,
  output [3:0] read_register_1,
  output [3:0] read_register_2,
  output [3:0] write_register,
  output [15:0] write_value
);

  wire xor_1_out;
  wire [0:0] and_1_out;

  and and_1 (and_1_out[0], flags_in[3], ~flags_in[4]);  // AND_Gate
  Multiplexer #(.width(16)) multiplexer_1 (
    .in0({read_value[14:0], and_1_out[0]}), .in1({{2{read_value[15]}}, read_value[14:1]}), .out(write_value),
    .sel(right));  // open: en
  Multiplexer multiplexer_2 (.in0(read_value[15]), .in1(read_value[0]), .out(flags_out[3]), .sel(right));  // open: en
  zero_sign zero_sign_1 (.in_1(write_value), .zero(flags_out[1]), .sign(flags_out[0]));
  xor xor_1 (xor_1_out, flags_out[0], read_value[15]);
  Multiplexer multiplexer_3 (.in0(xor_1_out), .in1(flags_in[2]), .out(flags_out[2]), .sel(right));  // open: en

  assign flags_out[4] = flags_in[4];
  assign read_register_1 = b;
  assign read_register_2 = 4'b0000;
  assign write_flags = 1'b1;
  assign write_register = d;

  // Other names for the same wires on the sheet: rv[15:0] = read_value; carry_in = flags_in[3];
  //   sign_out = flags_out[0]; zero_out = flags_out[1]; overflow_out = flags_out[2]; carry_out = flags_out[3];
  //   carry_block_in = flags_in[4]
endmodule

module SAVEF (
  input  [3:0] d,
  input  [4:0] flags_in,
  output write_flags,
  output [4:0] flags_out,
  output [3:0] read_register_1,
  output [3:0] read_register_2,
  output [3:0] write_register,
  output [15:0] write_value
);


  assign flags_out = {5{1'b0}};
  assign read_register_1 = 4'b0000;
  assign read_register_2 = 4'b0000;
  assign write_flags = 1'b0;
  assign write_register = d;
  assign write_value = {{11{1'b0}}, flags_in};
endmodule

module RSTRF (
  input  [3:0] d,
  input  [15:0] read_value,
  output write_flags,
  output [4:0] flags_out,
  output [3:0] read_register_1,
  output [3:0] read_register_2,
  output [3:0] write_register,
  output [15:0] write_value
);


  assign flags_out = read_value[4:0];
  assign read_register_1 = d;
  assign read_register_2 = 4'b0000;
  assign write_flags = 1'b1;
  assign write_register = 4'b0000;
  assign write_value = {16{1'b0}};
endmodule

module FON_FF (
  input  [3:0] _0_3,
  input  [3:0] _8_11,
  input  [4:0] flags_in,
  output write_flags,
  output [4:0] flags_out,
  output [3:0] read_register_1,
  output [3:0] read_register_2,
  output [3:0] write_register,
  output [15:0] write_value
);

  wire not_1_out;

  not not_1 (not_1_out, _8_11[3]);
  Multiplexer multiplexer_1 (.in0(flags_in[0]), .in1(not_1_out), .out(flags_out[0]), .sel(_0_3[0]));  // open: en
  Multiplexer multiplexer_2 (.in0(flags_in[1]), .in1(not_1_out), .out(flags_out[1]), .sel(_0_3[1]));  // open: en
  Multiplexer multiplexer_3 (.in0(flags_in[2]), .in1(not_1_out), .out(flags_out[2]), .sel(_0_3[2]));  // open: en
  Multiplexer multiplexer_4 (.in0(flags_in[3]), .in1(not_1_out), .out(flags_out[3]), .sel(_0_3[3]));  // open: en
  Multiplexer multiplexer_5 (.in0(flags_in[4]), .in1(not_1_out), .out(flags_out[4]), .sel(_8_11[0]));  // open: en

  assign read_register_1 = 4'b0000;
  assign read_register_2 = 4'b0000;
  assign write_flags = 1'b1;
  assign write_register = 4'b0000;
  assign write_value = {16{1'b0}};
endmodule

module FSET (
  input  [3:0] _0_3,
  input  [3:0] _8_11,
  input  [4:0] flags_in,
  output write_flags,
  output [4:0] flags_out,
  output [3:0] read_register_1,
  output [3:0] read_register_2,
  output [3:0] write_register,
  output [15:0] write_value
);

  Multiplexer multiplexer_1 (.in0(_8_11[0]), .in1(flags_in[4]), .out(flags_out[4]), .sel(_8_11[3]));  // open: en

  assign flags_out[3:0] = _0_3;
  assign read_register_1 = 4'b0000;
  assign read_register_2 = 4'b0000;
  assign write_flags = 1'b1;
  assign write_register = 4'b0000;
  assign write_value = {16{1'b0}};
endmodule

module LOAD (
  input  [3:0] d,
  input  [3:0] b,
  input  [4:0] o,
  input  [4:0] flags_in,
  input  [15:0] register_read_value,
  input  [15:0] memory_read_value,
  output write_flags,
  output [4:0] flags_out,
  output [3:0] read_register_1,
  output [3:0] read_register_2,
  output [3:0] write_register,
  output [15:0] write_value,
  output [15:0] memory_access_address
);

  zero_sign zero_sign_1 (.in_1(memory_read_value), .zero(flags_out[1]), .sign(flags_out[0]));
  Adder #(.width(16)) adder_1 (
    .a({{11{1'b0}}, o}), .b(register_read_value), .out(memory_access_address));  // open: cin, cout

  assign flags_out[4:2] = flags_in[4:2];
  assign read_register_1 = b;
  assign read_register_2 = 4'b0000;
  assign write_flags = 1'b1;
  assign write_register = d;
  assign write_value = memory_read_value;

  // Other names for the same wires on the sheet: sign_out = flags_out[0]; zero_out = flags_out[1]
endmodule

module STORE (
  input  [3:0] d,
  input  [3:0] b,
  input  [4:0] o,
  input  [15:0] register_read_value_1,
  input  [15:0] register_read_value_2,
  output write_flags,
  output [4:0] flags_out,
  output [3:0] read_register_1,
  output [3:0] read_register_2,
  output [3:0] write_register,
  output [15:0] write_value,
  output [15:0] memory_access_address
);

  Adder #(.width(16)) adder_1 (
    .a({{11{1'b0}}, o}), .b(register_read_value_2), .out(memory_access_address));  // open: cin, cout

  assign flags_out = {5{1'b0}};
  assign read_register_1 = d;
  assign read_register_2 = b;
  assign write_flags = 1'b0;
  assign write_register = 4'b0000;
  assign write_value = register_read_value_1;
endmodule

module INC_DEC (
  input  [3:0] d,
  input  [5:0] epsilon,
  input  DEC,
  input  [4:0] flags_in,
  input  [15:0] register_read_value_1,
  output write_flags,
  output [4:0] flags_out,
  output [3:0] read_register_1,
  output [3:0] read_register_2,
  output [3:0] write_register,
  output [15:0] write_value
);

  wire adder_1_cout, not_1_out, subtractor_1_bout;
  wire [15:0] adder_1_out, subtractor_1_out;

  Adder #(.width(16)) adder_1 (
    .a({{10{1'b0}}, epsilon}), .b(register_read_value_1), .out(adder_1_out), .cin(1'b1), .cout(adder_1_cout));
  Multiplexer #(.width(16)) multiplexer_1 (
    .in0(adder_1_out), .in1(subtractor_1_out), .out(write_value), .sel(DEC));  // open: en
  Subtractor #(.width(16)) subtractor_1 (
    .a(register_read_value_1), .b({{10{1'b0}}, epsilon}), .out(subtractor_1_out), .bin(1'b1),
    .bout(subtractor_1_bout));
  Multiplexer multiplexer_2 (.in0(adder_1_cout), .in1(not_1_out), .out(flags_out[3]), .sel(DEC));  // open: en
  not not_1 (not_1_out, subtractor_1_bout);
  zero_sign zero_sign_1 (.in_1(write_value), .zero(flags_out[1]), .sign(flags_out[0]));
  xor xor_1 (flags_out[2], write_value[15], register_read_value_1[15]);

  assign flags_out[4] = flags_in[4];
  assign read_register_1 = d;
  assign read_register_2 = 4'b0000;
  assign write_flags = 1'b1;
  assign write_register = d;

  // Other names for the same wires on the sheet: sign_out = flags_out[0]; zero_out = flags_out[1];
  //   overflow_out = flags_out[2]; carry_out = flags_out[3]; carry_block_in = flags_in[4]
endmodule

module BRANCH (
  input  ABSOLUTE,
  input  [3:0] CONDITION_CODE,
  input  [3:0] b,
  input  [7:0] o,
  input  [4:0] flags_in,
  input  [15:0] program_counter_in,
  input  [15:0] register_read_value,
  output write_flags,
  output [4:0] flags_out,
  output [3:0] read_register_1,
  output [3:0] read_register_2,
  output [3:0] write_register,
  output [15:0] write_value,
  output [15:0] PC_out
);

  wire BL_BGE_out, BLE_BG_out, BULE_BUG_out, multiplexer_1_out, not_1_out, not_2_out, not_3_out, not_4_out,
       not_5_out, not_6_out, not_7_out, xor_1_out;
  wire [15:0] adder_1_out, adder_2_out, multiplexer_2_out;

  xor BL_BGE (BL_BGE_out, flags_in[0], flags_in[2]);
  xor xor_1 (xor_1_out, flags_in[0], flags_in[2]);
  or BLE_BG (BLE_BG_out, xor_1_out, flags_in[1]);
  or BULE_BUG (BULE_BUG_out, ~flags_in[3], flags_in[1]);  // OR_Gate
  not not_1 (not_1_out, BL_BGE_out);
  not not_2 (not_2_out, BLE_BG_out);
  not not_3 (not_3_out, BULE_BUG_out);
  Multiplexer #(.select(4)) multiplexer_1 (
    .in0(1'b1), .in1(1'b0), .in2(BL_BGE_out), .in3(not_1_out), .in4(BLE_BG_out), .in5(not_2_out),
    .in6(BULE_BUG_out), .in7(not_3_out), .in8(flags_in[1]), .in9(not_4_out), .in10(flags_in[3]),
    .in11(not_5_out), .in12(flags_in[0]), .in13(not_6_out), .in14(flags_in[2]), .in15(not_7_out),
    .out(multiplexer_1_out), .sel(CONDITION_CODE));  // open: en
  not not_4 (not_4_out, flags_in[1]);
  not not_5 (not_5_out, flags_in[3]);
  not not_6 (not_6_out, flags_in[0]);
  not not_7 (not_7_out, flags_in[2]);
  Adder #(.width(16)) adder_1 (.a(program_counter_in), .b({{9{o[7]}}, o[6:0]}), .out(adder_1_out));  // open: cin, cout
  Adder #(.width(16)) adder_2 (.a(16'h1), .b(program_counter_in), .out(adder_2_out));  // open: cin, cout
  Multiplexer #(.width(16)) multiplexer_2 (
    .in0(adder_1_out), .in1(register_read_value), .out(multiplexer_2_out), .sel(ABSOLUTE));  // open: en
  Multiplexer #(.width(16)) multiplexer_3 (
    .in0(adder_2_out), .in1(multiplexer_2_out), .out(PC_out), .sel(multiplexer_1_out));  // open: en

  assign flags_out = {5{1'b0}};
  assign read_register_1 = b;
  assign read_register_2 = 4'b0000;
  assign write_flags = 1'b0;
  assign write_register = 4'b0000;
  assign write_value = {16{1'b0}};

  // Other names for the same wires on the sheet: ABS = ABSOLUTE; CC[3:0] = CONDITION_CODE; sign_in = flags_in[0];
  //   zero_in = flags_in[1]; overflow_in = flags_in[2]; carry_in = flags_in[3]; carry_block_in = flags_in[4];
  //   PC_in[15:0] = program_counter_in
endmodule

module CALL_RETURN (
  input  [3:0] b,
  input  [15:0] program_counter_in,
  input  [15:0] register_read_value,
  output write_flags,
  output [4:0] flags_out,
  output [3:0] read_register_1,
  output [3:0] read_register_2,
  output [3:0] write_register,
  output [15:0] write_value,
  output [15:0] PC_out
);

  Adder #(.width(16)) adder_1 (.a({16{1'b0}}), .b(program_counter_in), .out(write_value), .cin(1'b1));  // open: cout

  assign flags_out = {5{1'b0}};
  assign PC_out = register_read_value;
  assign read_register_1 = b;
  assign read_register_2 = 4'b0000;
  assign write_flags = 1'b0;
  assign write_register = b;

  // Other names for the same wires on the sheet: PC_in[15:0] = program_counter_in
endmodule
